# Fritzing sketch lights_controller_pcb_2 (saved by Fritzing 0.9.2b)
circuit board: 3.73822cm x 4.10001cm
breadboards: 1

parts:
  Q1 = NPN-Transistor [package="TO92 [THT]"]
  ESP01 = ESP01 Pin Header [form="♀ (female)" package=THT]
  Relay1 = 3V Songle Relay [package=relay-jzc]
  R1 = Resistor [tolerance=±5% resistance=220 package=THT]
  R2 = Resistor [tolerance=±5% resistance=10k package=THT]
  Terminal_Block = Screw terminal - 3 pins [package=THT]
  Fuse1 = Fuse with Handler [part_number=Htc-15m]
  R3 = Resistor [tolerance=±5% resistance=10k package=THT]
  3_3V_IN = Screw terminal - 2 pins [package=THT]
  220AC_OUT = Screw terminal - 2 pins [package=THT]
  D2 = Schottky Diode [part_number=1N5817 package="Melf DO-213 AB [SMD]"]

nets:
  N1: Q1.E, R2.Pin_0
  N2: Q1.B, R1.Pin_1
  N3: Q1.C, Relay1.COIL2, D2.anode
  N4: ESP01.RXD, R1.Pin_0
  N5: ESP01.VCC, ESP01.RST, ESP01.CH_PD, Relay1.COIL1, R3.Pin_1, 3_3V_IN.pin2, D2.cathode
  N6: ESP01.GPIO0, ESP01.GPIO2, R3.Pin_0
  N7: ESP01.GND, R2.Pin_1, 3_3V_IN.pin1
  N8: Relay1.COM, Fuse1.Connector2, 220AC_OUT.pin2
  N9: Relay1.NO, Terminal_Block.S
  N10: Terminal_Block.L, Fuse1.Connector1
  N11: Terminal_Block.N, 220AC_OUT.pin1

custom parts:
  ESP01 Pin Header: Pin Header for the ESP-01 ESP8266 board
  3V Songle Relay: SRD-0VDC-SL-C
  Screw terminal - 3 pins: Screw terminal with 3 pins
